// Logisim project RAMsito.circ as structural Verilog: 2 circuits, main circuit main
module main (
  input  nWE,
  input  nCS
);

  wire DIRECCIONES_sw1, DIRECCIONES_sw2, DIRECCIONES_sw3, DIRECCIONES_sw4, ENTRADA_sw1, ENTRADA_sw2,
       ENTRADA_sw3, ENTRADA_sw4, ENTRADA_sw5, ENTRADA_sw6, ENTRADA_sw7, ENTRADA_sw8;
  wire [3:0] memory_ram_1_s1, memory_ram_2_s1;

  DipSwitch ENTRADA (
    .sw1(ENTRADA_sw1), .sw2(ENTRADA_sw2), .sw3(ENTRADA_sw3), .sw4(ENTRADA_sw4), .sw5(ENTRADA_sw5),
    .sw6(ENTRADA_sw6), .sw7(ENTRADA_sw7), .sw8(ENTRADA_sw8));
  DipSwitch #(.number(4)) DIRECCIONES (
    .sw1(DIRECCIONES_sw1), .sw2(DIRECCIONES_sw2), .sw3(DIRECCIONES_sw3), .sw4(DIRECCIONES_sw4));
  memory_ram memory_ram_1 (
    .nWE(nWE), .nCS(nCS), .A0(DIRECCIONES_sw4), .A1(DIRECCIONES_sw3), .A2(DIRECCIONES_sw2),
    .A3(DIRECCIONES_sw1), .D0(ENTRADA_sw4), .D1(ENTRADA_sw3), .D2(ENTRADA_sw2), .D3(ENTRADA_sw1),
    .S1(memory_ram_1_s1[0]), .S2(memory_ram_1_s1[1]), .S3(memory_ram_1_s1[2]), .S4(memory_ram_1_s1[3]));
  memory_ram memory_ram_2 (
    .nWE(nWE), .nCS(nCS), .A0(DIRECCIONES_sw4), .A1(DIRECCIONES_sw3), .A2(DIRECCIONES_sw2),
    .A3(DIRECCIONES_sw1), .D0(ENTRADA_sw8), .D1(ENTRADA_sw7), .D2(ENTRADA_sw6), .D3(ENTRADA_sw5),
    .S1(memory_ram_2_s1[0]), .S2(memory_ram_2_s1[1]), .S3(memory_ram_2_s1[2]), .S4(memory_ram_2_s1[3]));
  Hex_Digit_Display #(.decimalPoint("false")) hex_digit_display_1 (.value(memory_ram_1_s1));
  Hex_Digit_Display #(.decimalPoint("false")) hex_digit_display_2 (.value(memory_ram_2_s1));
endmodule

module memory_ram (
  input  nWE,
  input  nCS,
  input  A0,
  input  A1,
  input  A2,
  input  A3,
  input  D0,
  input  D1,
  input  D2,
  input  D3,
  output S1,
  output S2,
  output S3,
  output S4
);

  wire and_1_out, and_2_out, CLK_out, not_1_out, not_2_out, not_3_out, not_4_out;
  wire [3:0] ram_1_dout;

  not not_1 (not_1_out, nWE);
  not not_2 (not_2_out, nCS);
  and and_1 (and_1_out, not_1_out, not_2_out);
  Clock CLK (.out(CLK_out));
  not not_3 (not_3_out, not_1_out);
  not not_4 (not_4_out, nCS);
  RAM #(.addrWidth(4), .dataWidth(4)) ram_1 (
    .addr({A3, A2, A1, A0}), .we(and_1_out), .oe(and_2_out), .clk(CLK_out), .din({D3, D2, D1, D0}),
    .dout(ram_1_dout));
  and and_2 (and_2_out, not_3_out, not_4_out);
  assign S1 = and_2_out ? ~ram_1_dout[0] : 1'bz;  // Controlled_Inverter controlled_inverter_1
  assign S2 = and_2_out ? ~ram_1_dout[1] : 1'bz;  // Controlled_Inverter controlled_inverter_2
  assign S3 = and_2_out ? ~ram_1_dout[2] : 1'bz;  // Controlled_Inverter controlled_inverter_3
  assign S4 = and_2_out ? ~ram_1_dout[3] : 1'bz;  // Controlled_Inverter controlled_inverter_4
  Hex_Digit_Display #(.decimalPoint("false")) hex_digit_display_1 (.value({S4, S3, S2, S1}));
endmodule
